# Fritzing sketch SmartPlant (saved by Fritzing 0.9.4)
breadboards: 1

parts:
  Argon1 = Particle Argon
  S1 = Pushbutton [package="[THT]"]
  S2 = Pushbutton [package="[THT]"]
  M1 = BMP280
  OLED_I2C1 = OLED 128x64 I2C Monochrome Display
  Q1 = PNP-Transistor [package="SOT-23 [SMD]"]
  R1 = Resistor [tolerance=±5% resistance=220 package=THT]
  R2 = Resistor [tolerance=±5% resistance=220 package=THT]
  Part1 = MQ-131 breakout  # not connected
  Grove1 = Grove Dust Sensor  # not connected
  Relay1 = Relay - 6 pins [package="DIP (Dual Inline) [THT]"]  # not connected
  SENS1 = SoilWatch 10  # not connected
  M2 = DC Motor  # not connected

nets:
  3.3V: Argon1.3.3V, S1.Pin_3, S1.Pin_4, S2.Pin_3, S2.Pin_4, M1.VIN, OLED_I2C1.VDD
  GND: Argon1.GND, M1.GND, OLED_I2C1.GND, Q1.1, R1.Pin_0
  N1: Argon1.MI, Q1.0, R1.Pin_1
  N2: Argon1.RX, S2.Pin_1, S2.Pin_2
  N3: Argon1.TX, S1.Pin_1
  N4: Argon1.SDA, M1.SDA, OLED_I2C1.SDA
  N5: Argon1.SCL, M1.SCL, OLED_I2C1.SCK
  N6: Argon1.VUSB, R2.Pin_1
  N7: Q1.2, R2.Pin_0

custom parts:
  Particle Argon: The Argon is a powerful Wi-Fi enabled development board that can act as either a standalone Wi-Fi endpoint or Wi-Fi enabled gateway for Particle Mesh networks. It is based on the Nordic nRF52840 and has built-in battery charging circuitry so it’s easy to connect a Li-Po and deploy your local network in minutes. The Argon is great for connecting existing projects to the Particle Device Cloud or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
  Pushbutton: A generic pushbutton.
  Pushbutton: A generic pushbutton.
  BMP280: Temperature Humidity Barometric presure Sensor, I2C
  MQ-131 breakout: SKU: 101282
  Grove Dust Sensor: PPD42 Grove Dust Sensor
  Relay - 6 pins: A DIP stand-in part for whatever IC you want. With 6 pins on a 900mil dual inline package (DIP) footprint.
  SoilWatch 10: SoilWatch 10 - Capacitive soil moisture sensor
